# Fritzing sketch Breadboard (saved by Fritzing 0.9.3b)
breadboards: 2

parts:
  Teensy_3_1 = Teensy 3.1
  Part1 = 3.5in TFT 480x320 Touch + MicroSD
  R1 = Resistor [tolerance=±5% resistance=10k package="0603 [SMD]"]
  DHT1 = DHT11 Humitidy and Temperature Sensor
  PWM_FAN = Header 4 [package=screwterminal-3.5mm-4_lock]
  12V_DC = Battery
  R2 = Resistor [tolerance=±5% resistance=1k package="0603 [SMD]"]
  C1 = Electrolytic Capacitor [capacitance=47µF package="0605 [SMD, electrolytic]"]
  S1 = Toggle Switch [package=THT]

nets:
  N1: Teensy_3_1.D1, R1.Pin_1
  N2: Teensy_3_1.D2, Part1.LCD_DATA0_5V
  N3: Teensy_3_1.D3, R2.Pin_1
  N4: Teensy_3_1.D4, S1.COM
  N5: Teensy_3_1.D5, Part1.LCD_DATA7_5V
  N6: Teensy_3_1.D6, Part1.LCD_DATA4_5V
  N7: Teensy_3_1.D7, Part1.LCD_DATA2_5V
  N8: Teensy_3_1.D8, Part1.LCD_DATA3_5V
  N9: Teensy_3_1.D9, Part1.RD
  N10: Teensy_3_1.D10, Part1.WR/SPI_CLK
  N11: Teensy_3_1.D11, Part1.C/D
  N12: Teensy_3_1.D12, Part1.CS
  N13: Teensy_3_1.A0/D14, Part1.LCD_X+, Part1.LCD_DATA1_5V
  N14: Teensy_3_1.A2/D16, Part1.LCD_Y+
  N15: Teensy_3_1.A3/D17, Part1.LCD_X-
  N16: Teensy_3_1.A4/D18, Part1.LCD_Y-
  N17: Teensy_3_1.A6/D20, Part1.LCD_DATA5_5V
  N18: Teensy_3_1.A7/D21, Part1.LCD_DATA6_5V
  N19: Part1.Backlite/Lite, S1.L1
  N20: R1.Pin_0, DHT1.DATA
  N21: DHT1.GND, C1.-
  N22: PWM_FAN.1, 12V_DC.+
  N23: PWM_FAN.2, R2.Pin_0, C1.+
  N24: PWM_FAN.4, 12V_DC.-

custom parts:
  3.5in TFT 480x320 Touch + MicroSD: This TFT display is big (3.5" diagonal), bright (6 white-LED backlight) and colorful! 480x320 pixels with individual RGB pixel control. This display also has a resistive touchscreen attached to it already, so you can detect finger presses anywhere on the screen. There is a controller built into the display with RAM buffering, so that almost no work is done by the microcontroller. The display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
  DHT11 Humitidy and Temperature Sensor: DHT11 Humidity and Temperature Sensor
